# Fritzing sketch Untitled Sketch 2 (saved by Fritzing 0.9.3b)
breadboards: 1

parts:
  Part1 = Arduino Uno (Rev3)
  Part2 = Arduino Uno (Rev3)
  Part3 = RFID-RC522-v2
  J1 = Piezo Speaker
  KY-1 = Keyes Relay [package=THT]
  Mod1 = KY-016 RGB Full Color LED Module [package="Breakout board"]
  VCC1 = Battery block 9V

nets:
  N1: Part1.D9_PWM, Part3.RST
  N2: Part1.D10_PWM/SS, Part3.SDA
  N3: Part1.D11_PWM/MOSI, Part3.MOSI
  N4: Part1.D12/MISO, Part3.MISO
  N5: Part1.D13/SCK, Part3.SCK
  GND: Part1.GND, Part3.GND
  N6: Part1.D0/RX, Part2.D1/TX
  N7: Part1.D1/TX, Part2.D0/RX
  3V3: Part1.3V3, Part3.3.3V
  N8: Part2.D9_PWM, J1.pin2
  N9: Part2.D2, Mod1.B
  N10: Part2.D3_PWM, Mod1.G
  N11: Part2.D4, Mod1.R
  N12: Part2.D7, KY-1.signal
  N13: Part2.5V, KY-1.power
  N14: Part2.GND, J1.pin1, KY-1.ground, Mod1.-
  N15: KY-1.NO, VCC1.+

notes:
  DOOR LOCK

custom parts:
  RFID-RC522-v2: A simple China made RFID-RC522 Reader; do check the pin labels, as this is a MFRC522 based clone.
  Keyes Relay: The Keyes 5V relay module is suitable for SCM development, home appliance control. It uses a 5V~12V TIL control signal which can control DC / AC signal.
  KY-016 RGB Full Color LED Module: KY-016 Arduino full color 5mm RGB LED, different colors can be obtained by mixing the three primary colors.
